// Logisim project ex5.circ as structural Verilog: 6 circuits, main circuit rotr
module rotr (
  input  [15:0] A,
  input  [3:0] B,
  output [15:0] Out1
);

  wire [15:0] multiplexer_1_out, multiplexer_2_out, multiplexer_3_out, rot1_1_out_2, rot2_1_out_2,
       rot4_1_out_2, rot8_1_out_2;

  rot8 rot8_1 (.in_1(A), .out_2(rot8_1_out_2));
  Multiplexer #(.width(16), .enable("false")) multiplexer_1 (
    .in0(A), .in1(rot8_1_out_2), .out(multiplexer_1_out), .sel(B[3]));
  rot4 rot4_1 (.in_1(multiplexer_1_out), .out_2(rot4_1_out_2));
  Multiplexer #(.width(16), .enable("false")) multiplexer_2 (
    .in0(multiplexer_1_out), .in1(rot4_1_out_2), .out(multiplexer_2_out), .sel(B[2]));
  rot2 rot2_1 (.in_1(multiplexer_2_out), .out_2(rot2_1_out_2));
  Multiplexer #(.width(16), .enable("false")) multiplexer_3 (
    .in0(multiplexer_2_out), .in1(rot2_1_out_2), .out(multiplexer_3_out), .sel(B[1]));
  rot1 rot1_1 (.in_1(multiplexer_3_out), .out_2(rot1_1_out_2));
  Multiplexer #(.width(16), .enable("false")) multiplexer_4 (
    .in0(multiplexer_3_out), .in1(rot1_1_out_2), .out(Out1), .sel(B[0]));

  // Notes on the sheet:
  //   PUT CIRCUITRY HERE
endmodule

module rot8 (
  input  [15:0] in_1,
  output [15:0] out_2
);


  assign out_2 = {in_1[7:0], in_1[15:8]};

  // Notes on the sheet:
  //   PUT CIRCUITRY HERE
endmodule

module rot4 (
  input  [15:0] in_1,
  output [15:0] out_2
);


  assign out_2 = {in_1[3:0], in_1[15:4]};

  // Notes on the sheet:
  //   PUT CIRCUITRY HERE
endmodule

module rot2 (
  input  [15:0] in_1,
  output [15:0] out_2
);


  assign out_2 = {in_1[1:0], in_1[15:2]};

  // Notes on the sheet:
  //   PUT CIRCUITRY HERE
endmodule

module rot1 (
  input  [15:0] in_1,
  output [15:0] out_2
);


  assign out_2 = {in_1[0], in_1[15:1]};

  // Notes on the sheet:
  //   PUT CIRCUITRY HERE
endmodule

module rightMove (
  input  [15:0] InputA,
  input  [3:0] InputB,
  output [15:0] out_3
);

  wire [3:0] multiplier_1_out;
  wire [15:0] bit_extender_1_out;

  Multiplier #(.width(4)) multiplier_1 (.a(4'b0010), .b(InputB), .out(multiplier_1_out));  // open: cin, cout
  assign bit_extender_1_out = {{12{multiplier_1_out[3]}}, multiplier_1_out};  // Bit_Extender bit_extender_1
  Divider #(.width(16)) divider_1 (.a(InputA), .b(bit_extender_1_out), .out(out_3));  // open: upper, rem
endmodule
