// Logisim project ex1.circ as structural Verilog: 3 circuits, main circuit main
module main (
  output [7:0] non_pipe_out,
  output [7:0] pipe_out
);

  wire CLK_out;
  wire [7:0] Address_Counter_q, rom_1_data;

  Counter Address_Counter (.clk(CLK_out), .Q(Address_Counter_q));  // open: clr, load, up, count, D, carry
  Clock CLK (.out(CLK_out));
  ROM rom_1 (.addr(Address_Counter_q), .data(rom_1_data));
  // Probe on non_pipe_out
  non_pipelined non_pipelined_1 (.in1(8'h1), .in2(rom_1_data), .CLK(CLK_out), .out1(non_pipe_out));
  // Probe on pipe_out
  pipelined pipelined_1 (.in1(8'h1), .in2(rom_1_data), .clk(CLK_out), .out1(pipe_out));

  // Notes on the sheet:
  //   contents of rom_1 (hex, n*v repeats v):
  //   3 2 fc 1 2 fb 1
endmodule

module non_pipelined (
  input  [7:0] in1,
  input  [7:0] in2,
  input  CLK,
  output [7:0] out1
);

  wire [7:0] adder_1_out, multiplier_1_out;

  Multiplier multiplier_1 (.a(in1), .b(in2), .out(multiplier_1_out));  // open: cin, cout
  Adder adder_1 (.a(multiplier_1_out), .b(out1), .out(adder_1_out));  // open: cin, cout
  Register register_1 (.D(adder_1_out), .clk(CLK), .Q(out1));  // open: en, clr

  // Notes on the sheet:
  //   60ns
  //   45ns
  //   10ns
  //   setup 10ns
  //   hold 10ns
endmodule

module pipelined (
  input  [7:0] in1,
  input  [7:0] in2,
  input  clk,
  output [7:0] out1
);

  wire [7:0] adder_1_out, multiplier_1_out, register_1_q;

  Multiplier multiplier_1 (.a(in1), .b(in2), .out(multiplier_1_out));  // open: cin, cout
  Register register_1 (.D(multiplier_1_out), .en(1'b1), .clk(clk), .Q(register_1_q));  // open: clr
  Adder adder_1 (.a(register_1_q), .b(out1), .out(adder_1_out));  // open: cin, cout
  Register register_2 (.D(adder_1_out), .en(1'b1), .clk(clk), .Q(out1));  // open: clr

  // Notes on the sheet:
  //   60ns
  //   10ns
  //   setup 10ns
  //   hold 10ns
  //   45ns
  //   10ns
  //   setup 10ns
  //   hold 10ns
endmodule
