// Logisim project regfile.circ as structural Verilog: 2 circuits, main circuit main
module main (
  input  [4:0] rs1,
  input  [4:0] rs2,
  input  [4:0] rd,
  input  [31:0] Write_Data,
  input  RegWEn,
  input  clk,
  output [31:0] ra,
  output [31:0] sp,
  output [31:0] t0,
  output [31:0] t1,
  output [31:0] t2,
  output [31:0] s0,
  output [31:0] s1,
  output [31:0] a0,
  output [31:0] Read_Data_1,
  output [31:0] Read_Data_2
);

  wire demultiplexer_1_out1, demultiplexer_1_out2, demultiplexer_1_out5, demultiplexer_1_out6,
       demultiplexer_1_out7, demultiplexer_1_out8, demultiplexer_1_out9, demultiplexer_1_out10;

  Demultiplexer #(.select(5), .enable("false")) demultiplexer_1 (
    .out1(demultiplexer_1_out1), .out2(demultiplexer_1_out2), .out5(demultiplexer_1_out5),
    .out6(demultiplexer_1_out6), .out7(demultiplexer_1_out7), .out8(demultiplexer_1_out8),
    .out9(demultiplexer_1_out9), .out10(demultiplexer_1_out10), .in(RegWEn), .sel(rd));  // open: out0, out3, out4, out11, out12, out13, out14, out15, out16, out17, out18, out19, out20, out21, out22, out23, out24, out25, out26, out27, out28, out29, out30, out31
  RegArc x1_ra (.InputD(Write_Data), .WriteEnable(demultiplexer_1_out1), .Clock(clk), .Data(ra));
  RegArc x2_sp (.InputD(Write_Data), .WriteEnable(demultiplexer_1_out2), .Clock(clk), .Data(sp));
  RegArc x5_t0 (.InputD(Write_Data), .WriteEnable(demultiplexer_1_out5), .Clock(clk), .Data(t0));
  RegArc x6_t1 (.InputD(Write_Data), .WriteEnable(demultiplexer_1_out6), .Clock(clk), .Data(t1));
  RegArc x7_t2 (.InputD(Write_Data), .WriteEnable(demultiplexer_1_out7), .Clock(clk), .Data(t2));
  RegArc x8_s0 (.InputD(Write_Data), .WriteEnable(demultiplexer_1_out8), .Clock(clk), .Data(s0));
  RegArc x9_s1 (.InputD(Write_Data), .WriteEnable(demultiplexer_1_out9), .Clock(clk), .Data(s1));
  RegArc x10_a0 (.InputD(Write_Data), .WriteEnable(demultiplexer_1_out10), .Clock(clk), .Data(a0));
  Multiplexer #(.select(5), .width(32), .enable("false")) multiplexer_1 (
    .in0({32{1'b0}}), .in1(ra), .in2(sp), .in5(t0), .in6(t1), .in7(t2), .in8(s0), .in9(s1), .in10(a0),
    .out(Read_Data_1), .sel(rs1));  // open: in3, in4, in11, in12, in13, in14, in15, in16, in17, in18, in19, in20, in21, in22, in23, in24, in25, in26, in27, in28, in29, in30, in31
  Multiplexer #(.select(5), .width(32), .enable("false")) multiplexer_2 (
    .in0({32{1'b0}}), .in1(ra), .in2(sp), .in5(t0), .in6(t1), .in7(t2), .in8(s0), .in9(s1), .in10(a0),
    .out(Read_Data_2), .sel(rs2));  // open: in3, in4, in11, in12, in13, in14, in15, in16, in17, in18, in19, in20, in21, in22, in23, in24, in25, in26, in27, in28, in29, in30, in31

  // Other names for the same wires on the sheet: read_data1[31:0] = Read_Data_1; read_data2[31:0] = Read_Data_2;
  //   read_reg1[4:0] = rs1; read_reg2[4:0] = rs2; write_en = RegWEn; write_reg[4:0] = rd

  // Notes on the sheet:
  //   INPUTS to your circuit
  //   DON'T CHANGE THE LOCATIONS OF THE INPUTS AND OUTPUTS!
  //   These are DEBUG/TEST outputs from your circuit.
  //   OUTPUTS from your circuit
endmodule

module RegArc (
  input  [31:0] InputD,
  input  WriteEnable,
  input  Clock,
  output [31:0] Data
);

  Register #(.width(32)) x1_ra (.D(InputD), .en(WriteEnable), .clk(Clock), .Q(Data));  // open: clr
endmodule
