// Logisim project alu.circ as structural Verilog: 17 circuits, main circuit alu
module alu (
  input  [31:0] A,
  input  [31:0] B,
  input  [3:0] ALUSel,
  output [31:0] Result
);

  wire [31:0] addsubc_1_o, andsubc_1_oupu, cntosubc_1_out_3, divsubc_1_o, divusubc_1_o, mulhsubc_1_o,
       mulhusubc_1_o, multsubc_1_o, orsubc_1_o, remusubc_1_o, sirsubc_1_o, sltsubc_1_o, srasubc_1_o,
       srllsubc_1_o, subsubc_1_o, xorsubc_1_o;

  andsubc andsubc_1 (.A(A), .B(B), .OUPU(andsubc_1_oupu));
  orsubc orsubc_1 (.A(A), .B(B), .O(orsubc_1_o));
  xorsubc xorsubc_1 (.A(A), .B(B), .O(xorsubc_1_o));
  addsubc addsubc_1 (.A(A), .B(B), .O(addsubc_1_o));
  subsubc subsubc_1 (.A(A), .B(B), .O(subsubc_1_o));
  multsubc multsubc_1 (.A(A), .B(B), .O(multsubc_1_o));
  mulhusubc mulhusubc_1 (.A(A), .B(B), .O(mulhusubc_1_o));
  mulhsubc mulhsubc_1 (.A(A), .B(B), .O(mulhsubc_1_o));
  divusubc divusubc_1 (.A(A), .B(B), .O(divusubc_1_o));
  divsubc divsubc_1 (.A(A), .B(B), .O(divsubc_1_o));
  remusubc remusubc_1 (.A(A), .B(B), .O(remusubc_1_o));
  srllsubc srllsubc_1 (.A(A), .B(B), .O(srllsubc_1_o));
  srasubc srasubc_1 (.A(A), .B(B), .O(srasubc_1_o));
  sltsubc sltsubc_1 (.A(A), .B(B), .O(sltsubc_1_o));
  sirsubc sirsubc_1 (.A(A), .B(B), .O(sirsubc_1_o));
  cntosubc cntosubc_1 (.in_1(A), .in_2(B), .out_3(cntosubc_1_out_3));
  Multiplexer #(.select(4), .width(32), .enable("false")) multiplexer_1 (
    .in0(andsubc_1_oupu), .in1(orsubc_1_o), .in2(xorsubc_1_o), .in3(addsubc_1_o), .in4(subsubc_1_o),
    .in5(multsubc_1_o), .in6(mulhusubc_1_o), .in7(mulhsubc_1_o), .in8(divusubc_1_o), .in9(divsubc_1_o),
    .in10(remusubc_1_o), .in11(srllsubc_1_o), .in12(srasubc_1_o), .in13(sltsubc_1_o), .in14(sirsubc_1_o),
    .in15(cntosubc_1_out_3), .out(Result), .sel(ALUSel));

  // Notes on the sheet:
  //   INPUTS to your circuit
  //   OUTPUT from your circuit
  //   DON'T CHANGE THE LOCATIONS OF THE INPUTS AND OUTPUTS!
endmodule

module andsubc (
  input  [31:0] A,
  input  [31:0] B,
  output [31:0] OUPU
);

  assign OUPU = A & B;  // AND_Gate and_1, 32 bits wide

  // Notes on the sheet:
  //   AND-0
endmodule

module addsubc (
  input  [31:0] A,
  input  [31:0] B,
  output [31:0] O
);

  Adder #(.width(32)) adder_1 (.a(A), .b(B), .out(O));  // open: cin, cout

  // Notes on the sheet:
  //   ADD-3
endmodule

module orsubc (
  input  [31:0] A,
  input  [31:0] B,
  output [31:0] O
);

  assign O = A | B;  // OR_Gate or_1, 32 bits wide

  // Notes on the sheet:
  //   OR-1
endmodule

module xorsubc (
  input  [31:0] A,
  input  [31:0] B,
  output [31:0] O
);

  wire [31:0] and_1_out, not_1_out, or_1_out;

  assign or_1_out = A | B;  // OR_Gate or_1, 32 bits wide
  assign and_1_out = B & A;  // AND_Gate and_1, 32 bits wide
  assign not_1_out = ~and_1_out;  // NOT_Gate not_1, 32 bits wide
  assign O = or_1_out & not_1_out;  // AND_Gate and_2, 32 bits wide

  // Notes on the sheet:
  //   XOR-2
endmodule

module subsubc (
  input  [31:0] A,
  input  [31:0] B,
  output [31:0] O
);

  Subtractor #(.width(32)) subtractor_1 (.a(A), .b(B), .out(O));  // open: bin, bout

  // Notes on the sheet:
  //   SUB-4
endmodule

module multsubc (
  input  [31:0] A,
  input  [31:0] B,
  output [31:0] O
);

  Multiplier #(.width(32)) multiplier_1 (.a(A), .b(B), .out(O));  // open: cin, cout

  // Notes on the sheet:
  //   MULT-5
endmodule

module mulhusubc (
  input  [31:0] A,
  input  [31:0] B,
  output [31:0] O
);

  Multiplier #(.width(32)) multiplier_1 (.a(A), .b(B), .cout(O));  // open: out, cin

  // Notes on the sheet:
  //   MULHU-6
endmodule

module mulhsubc (
  input  [31:0] A,
  input  [31:0] B,
  output [31:0] O
);

  wire [31:0] adder_1_out, multiplexer_1_out, multiplexer_2_out, multiplier_1_cout, multiplier_2_out,
       multiplier_3_out;

  Multiplier #(.width(32)) multiplier_1 (.a(A), .b(B), .cout(multiplier_1_cout));  // open: out, cin
  Multiplier #(.width(32)) multiplier_2 (.a({32{1'b1}}), .b(B), .out(multiplier_2_out));  // open: cin, cout
  Multiplier #(.width(32)) multiplier_3 (.a(A), .b({32{1'b1}}), .out(multiplier_3_out));  // open: cin, cout
  Multiplexer #(.width(32), .enable("false")) multiplexer_1 (
    .in0({32{1'b0}}), .in1(multiplier_2_out), .out(multiplexer_1_out), .sel(A[31]));
  Multiplexer #(.width(32), .enable("false")) multiplexer_2 (
    .in0({32{1'b0}}), .in1(multiplier_3_out), .out(multiplexer_2_out), .sel(B[31]));
  Adder #(.width(32)) adder_1 (.a(multiplier_1_cout), .b(multiplexer_2_out), .out(adder_1_out));  // open: cin, cout
  Adder #(.width(32)) adder_2 (.a(multiplexer_1_out), .b(adder_1_out), .out(O));  // open: cin, cout

  // Notes on the sheet:
  //   MULH-7
endmodule

module divusubc (
  input  [31:0] A,
  input  [31:0] B,
  output [31:0] O
);

  wire comparator_1_eq;
  wire [31:0] divider_1_out;

  Divider #(.width(32)) divider_1 (.a(A), .b(B), .out(divider_1_out));  // open: upper, rem
  Comparator #(.width(32)) comparator_1 (.a(B), .b({32{1'b0}}), .eq(comparator_1_eq));  // open: gt, lt
  Multiplexer #(.width(32), .enable("false")) multiplexer_1 (
    .in0(divider_1_out), .in1({32{1'b1}}), .out(O), .sel(comparator_1_eq));

  // Notes on the sheet:
  //   DIVU-8
endmodule

module divsubc (
  input  [31:0] A,
  input  [31:0] B,
  output [31:0] O
);

  wire comparator_1_eq;
  wire [31:0] bit_extender_1_out, bit_extender_2_out, divider_1_out, multiplexer_1_out, multiplexer_2_out,
       multiplexer_3_out, negator_1_out, negator_2_out, negator_3_out, xorsubc_1_o;

  Negator #(.width(32)) negator_1 (.in(A), .out(negator_1_out));
  Negator #(.width(32)) negator_2 (.in(B), .out(negator_2_out));
  Multiplexer #(.width(32), .enable("false")) multiplexer_1 (
    .in0(A), .in1(negator_1_out), .out(multiplexer_1_out), .sel(A[31]));
  Multiplexer #(.width(32), .enable("false")) multiplexer_2 (
    .in0(B), .in1(negator_2_out), .out(multiplexer_2_out), .sel(B[31]));
  Divider #(.width(32)) divider_1 (
    .a(multiplexer_1_out), .b(multiplexer_2_out), .out(divider_1_out));  // open: upper, rem
  assign bit_extender_1_out = {{31{A[31]}}, A[31]};  // Bit_Extender bit_extender_1
  assign bit_extender_2_out = {{31{B[31]}}, B[31]};  // Bit_Extender bit_extender_2
  xorsubc xorsubc_1 (.A(bit_extender_1_out), .B(bit_extender_2_out), .O(xorsubc_1_o));
  Negator #(.width(32)) negator_3 (.in(divider_1_out), .out(negator_3_out));
  Multiplexer #(.width(32), .enable("false")) multiplexer_3 (
    .in0(divider_1_out), .in1(negator_3_out), .out(multiplexer_3_out), .sel(xorsubc_1_o[0]));
  Divider #(.width(32)) divider_2 ();  // open: a, b, out, upper, rem
  Multiplexer #(.width(32), .enable("false")) multiplexer_4 (
    .in0(multiplexer_3_out), .in1({32{1'b1}}), .out(O), .sel(comparator_1_eq));
  Comparator #(.width(32)) comparator_1 (.a(B), .b({32{1'b0}}), .eq(comparator_1_eq));  // open: gt, lt

  // Other names for the same wires on the sheet: sb1 = A[31]; sb2 = B[31]

  // Notes on the sheet:
  //   DIV-9
endmodule

module remusubc (
  input  [31:0] A,
  input  [31:0] B,
  output [31:0] O
);

  wire [31:0] divider_1_out, multiplier_1_out;

  Divider #(.width(32)) divider_1 (.a(A), .b(B), .out(divider_1_out));  // open: upper, rem
  Multiplier #(.width(32)) multiplier_1 (.a(divider_1_out), .b(B), .out(multiplier_1_out));  // open: cin, cout
  Divider #(.width(32)) divider_2 (.a(A), .b(B), .rem(O));  // open: out, upper
  Subtractor #(.width(32)) subtractor_1 (.a(A), .b(multiplier_1_out));  // open: out, bin, bout

  // Notes on the sheet:
  //   REMU-10
endmodule

module srllsubc (
  input  [31:0] A,
  input  [31:0] B,
  output [31:0] O
);

  Shifter #(.width(32), .shift("lr")) shifter_1 (.in(A), .\dist (B[4:0]), .out(O));

  // Notes on the sheet:
  //   SRL-11
endmodule

module srasubc (
  input  [31:0] A,
  input  [31:0] B,
  output [31:0] O
);

  Shifter #(.width(32), .shift("ar")) shifter_1 (.in(A), .\dist (B[4:0]), .out(O));

  // Notes on the sheet:
  //   SRA-12
endmodule

module sltsubc (
  input  [31:0] A,
  input  [31:0] B,
  output [31:0] O
);

  wire comparator_1_lt;

  Comparator #(.width(32)) comparator_1 (.a(A), .b(B), .lt(comparator_1_lt));  // open: gt, eq
  assign O = {{31{1'b0}}, comparator_1_lt};  // Bit_Extender bit_extender_1

  // Notes on the sheet:
  //   slt-13
endmodule

module sirsubc (
  input  [31:0] A,
  input  [31:0] B,
  output [31:0] O
);

  wire comparator_1_eq;

  assign O = {{31{1'b0}}, comparator_1_eq};  // Bit_Extender bit_extender_1
  Comparator #(.width(32)) comparator_1 (
    .a({A[0], A[1], A[2], A[3], A[4], A[5], A[6], A[7], A[8], A[9], A[10], A[11], A[12], A[13], A[14], A[15], A[16], A[17], A[18], A[19], A[20], A[21], A[22], A[23], A[24], A[25], A[26], A[27], A[28], A[29], A[30], A[31]}),
    .b(B), .eq(comparator_1_eq));  // open: gt, lt

  // Notes on the sheet:
  //   sir-14
endmodule

module cntosubc (
  input  [31:0] in_1,
  input  [31:0] in_2,
  output [31:0] out_3
);

  Shifter #(.width(32)) shifter_1 (.in(in_1), .\dist (in_2[4:0]), .out(out_3));

  // Notes on the sheet:
  //   SLL-11
endmodule
