// Logisim project cpu.circ as structural Verilog: 17 circuits, main circuit main
module main (
  input  [31:0] INSTRUCTION,
  input  in_2,
  output [31:0] FETCH_ADDRESS,
  output [31:0] ra,
  output [31:0] sp,
  output [31:0] t0,
  output [31:0] t1,
  output [31:0] t2,
  output [31:0] s0,
  output [31:0] s1,
  output [31:0] a0
);

  wire aluinsel_1_downsel, Bresult, comparator_1_lt, comparator_2_eq, comparator_2_lt, comparator_3_eq,
       comparator_3_gt, comparator_3_lt, fixjumpadd_1_isfixadd, fixlui_1_luio, isauipc_1_isauipc, isjump,
       isPCtaken, iswriteramen_1_iswriteramen, nextaddress_1_isalu2pc, not_1_out, or_1_out, RegwriteEn;
  wire [1:0] wbsel_1_wbsel;
  wire [2:0] br_selbit_1_br;
  wire [3:0] alusel_1_alusel;
  wire [4:0] rd, rs1, rs2;
  wire [31:0] adder_1_out, ALU_result, DMEM_readdata, fixra_1_rs1fixra, imm, INSTRUCTION_t,
       loadramnotwordfix_1_loaddata, multiplexer_1_out, multiplexer_2_out, multiplexer_3_out,
       multiplexer_4_out, multiplexer_5_out, multiplexer_6_out, multiplexer_7_out, multiplier_1_out,
       register_2_q, rs1Data, rs2Data, shifter_1_out, shifter_2_out, subtractor_1_out, writeData;

  Adder #(.width(32)) adder_1 (.a(FETCH_ADDRESS), .b(32'h1), .out(adder_1_out));  // open: cin, cout
  Multiplexer #(.width(32), .enable("false")) multiplexer_1 (
    .in0(ALU_result), .out(multiplexer_1_out), .sel(comparator_1_lt));  // open: in1
  Comparator #(.width(32)) comparator_1 (.a(ALU_result), .b({32{1'b0}}), .lt(comparator_1_lt));  // open: gt, eq
  Subtractor #(.width(32)) subtractor_1 (.a(FETCH_ADDRESS), .b(32'h1), .out(subtractor_1_out));  // open: bin, bout
  Multiplexer #(.width(32), .enable("false")) multiplexer_2 (
    .in0(adder_1_out), .in1(multiplexer_1_out), .out(multiplexer_2_out), .sel(nextaddress_1_isalu2pc));
  nextAddress nextaddress_1 (.command(INSTRUCTION_t), .isBtrue(Bresult), .isAlu2PC(nextaddress_1_isalu2pc));
  Multiplexer #(.width(32), .enable("false")) multiplexer_3 (
    .in0(subtractor_1_out), .in1(shifter_1_out), .out(multiplexer_3_out), .sel(isauipc_1_isauipc));
  Shifter #(.width(32)) shifter_1 (.in(subtractor_1_out), .\dist (5'b00010), .out(shifter_1_out));
  isauipc isauipc_1 (.command(INSTRUCTION_t), .isauipc(isauipc_1_isauipc));
  Shifter #(.width(32), .shift("ar")) shifter_2 (.in(imm), .\dist (5'b00010), .out(shifter_2_out));
  Register #(.width(32)) PC (.D(multiplexer_2_out), .clk(in_2), .Q(FETCH_ADDRESS));  // open: en, clr
  regwen regwen_1 (.in_1(INSTRUCTION_t), .regwen(RegwriteEn));
  Multiplexer #(.width(32), .enable("false")) multiplexer_4 (
    .in0(imm), .in1(shifter_2_out), .out(multiplexer_4_out), .sel(fixjumpadd_1_isfixadd));
  Register #(.width(1)) register_1 (.D(nextaddress_1_isalu2pc), .clk(in_2), .Q(isjump));  // open: en, clr
  regfile_main RegFile (
    .rs2(rs2), .rd(rd), .Read_Data_1(rs1Data), .Read_Data_2(rs2Data), .ra(ra), .sp(sp), .t0(t0), .t1(t1),
    .t2(t2), .s0(s0), .s1(s1), .a0(a0), .rs1(rs1), .Write_Data(writeData), .RegWEn(RegwriteEn), .clk(in_2));
  Multiplexer #(.width(32), .enable("false")) multiplexer_5 (
    .in0(rs1Data), .in1(multiplexer_3_out), .out(multiplexer_5_out), .sel(isPCtaken));
  Multiplexer #(.width(32), .enable("false")) multiplexer_6 (
    .in0(rs2Data), .in1(multiplexer_4_out), .out(multiplexer_6_out), .sel(aluinsel_1_downsel));
  fixJumpAdd fixjumpadd_1 (.command(INSTRUCTION_t), .isPCtaken(isPCtaken), .isFixAdd(fixjumpadd_1_isfixadd));
  ALUINSEL aluinsel_1 (.COMMAND(INSTRUCTION_t), .UPSEL(isPCtaken), .DOWNSEL(aluinsel_1_downsel));
  alusel alusel_1 (.command(INSTRUCTION_t), .alusel(alusel_1_alusel));
  fixlui fixlui_1 (.command(INSTRUCTION_t), .luio(fixlui_1_luio));
  Register #(.width(32)) register_2 (.D(INSTRUCTION), .clk(in_2), .Q(register_2_q));  // open: en, clr
  Multiplexer #(.width(32), .enable("false")) multiplexer_7 (
    .in0({32{1'b0}}), .in1(multiplexer_5_out), .out(multiplexer_7_out), .sel(fixlui_1_luio));
  fixRa fixra_1 (.rs1data(multiplexer_7_out), .Command(INSTRUCTION_t), .rs1fixRa(fixra_1_rs1fixra));
  alu Arithmetic_Logic_Unit (
    .A(fixra_1_rs1fixra), .B(multiplexer_6_out), .ALUSel(alusel_1_alusel), .Result(ALU_result));
  dropInvaildCommand dropinvaildcommand_1 (.command(register_2_q), .isJump(isjump), .VaildCommand(INSTRUCTION_t));
  RegisterCommandDecode registercommanddecode_1 (.COMMAND(INSTRUCTION_t), .rd(rd), .rs1(rs1), .rs2(rs2));
  immGenerator immgenerator_1 (.COMMAND(INSTRUCTION_t), .immediate(imm));
  Comparator #(.width(32)) comparator_2 (
    .a(rs1Data), .b(rs2Data), .eq(comparator_2_eq), .lt(comparator_2_lt));  // open: gt
  Comparator #(.width(32), .mode("unsigned")) comparator_3 (
    .a(rs1Data), .b(rs2Data), .gt(comparator_3_gt), .eq(comparator_3_eq), .lt(comparator_3_lt));
  isWriteRAMEn iswriteramen_1 (.command(INSTRUCTION_t), .isWriteRAMEN(iswriteramen_1_iswriteramen));
  not not_1 (not_1_out, comparator_2_eq);
  or or_1 (or_1_out, comparator_3_gt, comparator_3_eq);
  BR_selbit br_selbit_1 (.command(INSTRUCTION_t), .BR(br_selbit_1_br));
  Multiplexer #(.select(3), .enable("false")) multiplexer_8 (
    .in0(comparator_2_eq), .in1(comparator_2_lt), .in2(comparator_3_lt), .in3(not_1_out), .in4(or_1_out),
    .out(Bresult), .sel(br_selbit_1_br));  // open: in5, in6, in7
  mem_main DMEM (
    .WriteAddr(ALU_result), .WriteData(rs2Data), .MemRW(iswriteramen_1_iswriteramen),
    .ReadData(DMEM_readdata), .clk(in_2));
  Multiplier #(.width(32)) multiplier_1 (.a(FETCH_ADDRESS), .b(32'h4), .out(multiplier_1_out));  // open: cin, cout
  loadRAMnotWordFix loadramnotwordfix_1 (
    .command(INSTRUCTION_t), .RAMData(DMEM_readdata), .loadData(loadramnotwordfix_1_loaddata));
  Multiplexer #(.select(2), .width(32), .enable("false")) multiplexer_9 (
    .in0(loadramnotwordfix_1_loaddata), .in1(ALU_result), .in2(multiplier_1_out), .out(writeData),
    .sel(wbsel_1_wbsel));  // open: in3
  wbsel wbsel_1 (.command(INSTRUCTION_t), .clock(in_2), .ifbtrue(Bresult), .wbsel(wbsel_1_wbsel));

  // Other names for the same wires on the sheet: clk = in_2; fetch_addr[31:0] = FETCH_ADDRESS;
  //   PC4[31:0] = FETCH_ADDRESS; INSTRUCTION1[31:0] = INSTRUCTION

  // Notes on the sheet:
  //   Output
  //   Inputs/Outputs from run.circ. DO NOT MOVE THESE.
  //   Inputs
  //   Inputs/Outputs from run.circ. DO NOT MOVE THESE.
endmodule

module RegisterCommandDecode (
  input  [31:0] COMMAND,
  output [4:0] rd,
  output [4:0] rs1,
  output [4:0] rs2
);


  assign rd = COMMAND[11:7];
  assign rs1 = COMMAND[19:15];
  assign rs2 = COMMAND[24:20];
endmodule

module immGenerator (
  input  [31:0] COMMAND,
  output [31:0] immediate
);

  wire [2:0] typediver_1_opcodetype;
  wire [31:0] bit_extender_1_out, bit_extender_2_out, bit_extender_3_out, bit_extender_4_out,
       bit_extender_5_out, shifter_1_out;

  assign bit_extender_1_out = {{12{COMMAND[31]}}, COMMAND[31:12]};  // Bit_Extender bit_extender_1
  Shifter #(.width(32)) shifter_1 (.in(bit_extender_1_out), .\dist (5'b01100), .out(shifter_1_out));
  assign bit_extender_2_out = {{20{COMMAND[31]}}, COMMAND[31:20]};  // Bit_Extender bit_extender_2
  assign bit_extender_3_out = {{20{COMMAND[31]}}, {COMMAND[31:25], COMMAND[11:7]}};  // Bit_Extender bit_extender_3
  assign bit_extender_4_out = {{19{COMMAND[31]}}, {COMMAND[31], COMMAND[7], COMMAND[30:25], COMMAND[11:8], 1'b0}};  // Bit_Extender bit_extender_4
  assign bit_extender_5_out = {{11{COMMAND[31]}}, {COMMAND[31], COMMAND[19:12], COMMAND[20], COMMAND[30:21], 1'b0}};  // Bit_Extender bit_extender_5
  typeDiver typediver_1 (.COMMAND(COMMAND), .opcodeType(typediver_1_opcodetype));
  Multiplexer #(.select(3), .width(32), .enable("false")) multiplexer_1 (
    .in0({32{1'b0}}), .in1(bit_extender_2_out), .in2(bit_extender_3_out), .in3(bit_extender_4_out),
    .in4(shifter_1_out), .in5(bit_extender_5_out), .out(immediate), .sel(typediver_1_opcodetype));  // open: in6, in7

  // Other names for the same wires on the sheet: com[31:0] = COMMAND; fun7[6:0] = COMMAND[31:25];
  //   fun3[2:0] = COMMAND[14:12]; opcode[6:0] = COMMAND[6:0]
endmodule

module typeDiver (
  input  [31:0] COMMAND,
  output [2:0] opcodeType
);

  wire comparator_1_eq, comparator_2_eq, comparator_3_eq, comparator_4_eq, comparator_5_eq, comparator_6_eq,
       comparator_7_eq, comparator_8_eq, comparator_9_eq, or_1_out, or_2_out, or_3_out;

  Comparator #(.width(7)) comparator_1 (.a(COMMAND[6:0]), .b(7'b1100111), .eq(comparator_1_eq));  // open: gt, lt
  Comparator #(.width(7)) comparator_2 (.a(7'b0100011), .b(COMMAND[6:0]), .eq(comparator_2_eq));  // open: gt, lt
  Comparator #(.width(7)) comparator_3 (.a(7'b1100011), .b(COMMAND[6:0]), .eq(comparator_3_eq));  // open: gt, lt
  Comparator #(.width(7)) comparator_4 (.a(7'b0110111), .b(COMMAND[6:0]), .eq(comparator_4_eq));  // open: gt, lt
  Comparator #(.width(7)) comparator_5 (.a(COMMAND[6:0]), .b(7'b0010111), .eq(comparator_5_eq));  // open: gt, lt
  Comparator #(.width(7)) comparator_6 (.a(7'b1101111), .b(COMMAND[6:0]), .eq(comparator_6_eq));  // open: gt, lt
  Comparator #(.width(7)) comparator_7 (.a(7'b0110011), .b(COMMAND[6:0]), .eq(comparator_7_eq));  // open: gt, lt
  Comparator #(.width(7)) comparator_8 (.a(7'b0000011), .b(COMMAND[6:0]), .eq(comparator_8_eq));  // open: gt, lt
  Comparator #(.width(7)) comparator_9 (.a(COMMAND[6:0]), .b(7'b0010011), .eq(comparator_9_eq));  // open: gt, lt
  or or_1 (or_1_out, comparator_4_eq, comparator_5_eq);
  or or_2 (or_2_out, comparator_8_eq, comparator_9_eq);
  or or_3 (or_3_out, or_2_out, comparator_1_eq);
  Priority_Encoder priority_encoder_1 (
    .in0(comparator_7_eq), .in1(or_3_out), .in2(comparator_2_eq), .in3(comparator_3_eq), .in4(or_1_out),
    .in5(comparator_6_eq), .out(opcodeType));  // open: in6, in7, en_in, gs, en_out

  // Other names for the same wires on the sheet: com[31:0] = COMMAND; opcode[6:0] = COMMAND[6:0];
  //   fun3[2:0] = COMMAND[14:12]; fun7[6:0] = COMMAND[31:25]
endmodule

module BR_selbit (
  input  [31:0] command,
  output [2:0] BR
);

  wire comparator_1_eq, comparator_2_eq, comparator_3_eq, comparator_4_eq, comparator_5_eq;

  Comparator #(.width(3)) comparator_1 (.a(3'b000), .b(command[14:12]), .eq(comparator_1_eq));  // open: gt, lt
  Comparator #(.width(3)) comparator_2 (.a(3'b100), .b(command[14:12]), .eq(comparator_2_eq));  // open: gt, lt
  Comparator #(.width(3)) comparator_3 (.a(3'b110), .b(command[14:12]), .eq(comparator_3_eq));  // open: gt, lt
  Comparator #(.width(3)) comparator_4 (.a(3'b001), .b(command[14:12]), .eq(comparator_4_eq));  // open: gt, lt
  Comparator #(.width(3)) comparator_5 (.a(3'b111), .b(command[14:12]), .eq(comparator_5_eq));  // open: gt, lt
  Priority_Encoder priority_encoder_1 (
    .in0(comparator_1_eq), .in1(comparator_2_eq), .in2(comparator_3_eq), .in3(comparator_4_eq),
    .in4(comparator_5_eq), .out(BR));  // open: in5, in6, in7, en_in, gs, en_out

  // Other names for the same wires on the sheet: com[31:0] = command; opcode[6:0] = command[6:0];
  //   fun3[2:0] = command[14:12]; fun7[6:0] = command[31:25]
endmodule

module ALUINSEL (
  input  [31:0] COMMAND,
  output UPSEL,
  output DOWNSEL
);

  wire [2:0] typediver_1_opcodetype;

  typeDiver typediver_1 (.COMMAND(COMMAND), .opcodeType(typediver_1_opcodetype));
  Multiplexer #(.select(3), .enable("false")) multiplexer_1 (
    .in0(1'b0), .in1(1'b0), .in2(1'b0), .in3(1'b1), .in4(1'b1), .in5(1'b1), .out(UPSEL),
    .sel(typediver_1_opcodetype));  // open: in6, in7
  Multiplexer #(.select(3), .enable("false")) multiplexer_2 (
    .in0(1'b0), .in1(1'b1), .in2(1'b1), .in3(1'b1), .in4(1'b1), .in5(1'b1), .out(DOWNSEL),
    .sel(typediver_1_opcodetype));  // open: in6, in7
endmodule

module alusel (
  input  [31:0] command,
  output [3:0] alusel
);

  wire adds, and_2_out, and_3_out, and_4_out, and_5_out, and_6_out, and_7_out, and_8_out, and_9_out,
       and_10_out, and_11_out, and_12_out, and_13_out, and_14_out, and_15_out, and_16_out, and_17_out,
       and_18_out, and_19_out, and_20_out, and_21_out, and_22_out, and_23_out, and_31_out, and_32_out,
       and_33_out, and_34_out, ands, comparator_1_eq, comparator_2_eq, comparator_3_eq, comparator_4_eq,
       comparator_5_eq, comparator_6_eq, comparator_7_eq, comparator_8_eq, comparator_9_eq, comparator_10_eq,
       comparator_11_eq, comparator_12_eq, comparator_13_eq, comparator_14_eq, comparator_15_eq,
       comparator_16_eq, comparator_17_eq, comparator_18_eq, comparator_19_eq, comparator_20_eq,
       comparator_21_eq, comparator_22_gt, comparator_23_eq, comparator_24_eq, comparator_25_eq,
       comparator_26_eq, comparator_27_eq, comparator_28_eq, comparator_29_eq, comparator_30_eq,
       comparator_31_eq, comparator_32_eq, comparator_33_eq, comparator_34_eq, comparator_35_eq,
       comparator_36_eq, comparator_37_eq, comparator_38_eq, comparator_39_eq, comparator_40_eq,
       comparator_41_eq, comparator_42_eq, comparator_43_eq, comparator_44_eq, comparator_45_eq,
       comparator_46_eq, comparator_47_eq, comparator_48_eq, comparator_49_eq, comparator_50_eq,
       comparator_51_eq, comparator_52_eq, comparator_53_eq, comparator_54_eq, comparator_55_eq,
       comparator_56_eq, comparator_57_eq, divs, divus, mulhs, mulhus, mults, or_1_out, or_5_out, or_8_out,
       ors, remus, slls, slts, srls, subs, xors;
  wire [2:0] comtype;

  // AND_Gate and_1 is placed but not wired
  Comparator #(.width(3)) comparator_1 (.a(comtype), .b(3'b000), .eq(comparator_1_eq));  // open: gt, lt
  Comparator #(.width(3)) comparator_2 (.a(command[14:12]), .b(3'b111), .eq(comparator_2_eq));  // open: gt, lt
  Comparator #(.width(7)) comparator_3 (.a(command[31:25]), .b({7{1'b0}}), .eq(comparator_3_eq));  // open: gt, lt
  Comparator #(.width(3)) comparator_4 (.a(comtype), .b(3'b001), .eq(comparator_4_eq));  // open: gt, lt
  Comparator #(.width(3)) comparator_5 (.a(command[14:12]), .b(3'b111), .eq(comparator_5_eq));  // open: gt, lt
  Comparator #(.width(3)) comparator_6 (.a(comtype), .b(3'b000), .eq(comparator_6_eq));  // open: gt, lt
  Comparator #(.width(3)) comparator_7 (.a(command[14:12]), .b(3'b110), .eq(comparator_7_eq));  // open: gt, lt
  Comparator #(.width(7)) comparator_8 (.a(command[31:25]), .b({7{1'b0}}), .eq(comparator_8_eq));  // open: gt, lt
  Comparator #(.width(3)) comparator_9 (.a(comtype), .b(3'b001), .eq(comparator_9_eq));  // open: gt, lt
  Comparator #(.width(3)) comparator_10 (.a(command[14:12]), .b(3'b110), .eq(comparator_10_eq));  // open: gt, lt
  Comparator #(.width(3)) comparator_11 (.a(comtype), .b(3'b000), .eq(comparator_11_eq));  // open: gt, lt
  Comparator #(.width(3)) comparator_12 (.a(command[14:12]), .b(3'b100), .eq(comparator_12_eq));  // open: gt, lt
  Comparator #(.width(7)) comparator_13 (.a(command[31:25]), .b({7{1'b0}}), .eq(comparator_13_eq));  // open: gt, lt
  Comparator #(.width(7)) comparator_14 (.a(command[6:0]), .b(7'b0010011), .eq(comparator_14_eq));  // open: gt, lt
  Comparator #(.width(3)) comparator_15 (.a(command[14:12]), .b(3'b100), .eq(comparator_15_eq));  // open: gt, lt
  Comparator #(.width(3)) comparator_16 (.a(comtype), .b(3'b000), .eq(comparator_16_eq));  // open: gt, lt
  Comparator #(.width(3)) comparator_17 (.a(command[14:12]), .b(3'b000), .eq(comparator_17_eq));  // open: gt, lt
  Comparator #(.width(7)) comparator_18 (.a(command[31:25]), .b({7{1'b0}}), .eq(comparator_18_eq));  // open: gt, lt
  Comparator #(.width(3)) comparator_19 (.a(comtype), .b(3'b001), .eq(comparator_19_eq));  // open: gt, lt
  Comparator #(.width(3)) comparator_20 (.a(command[14:12]), .b(3'b000), .eq(comparator_20_eq));  // open: gt, lt
  Comparator #(.width(7)) comparator_21 (.a(command[6:0]), .b(7'b0000011), .eq(comparator_21_eq));  // open: gt, lt
  Comparator #(.width(3), .mode("unsigned")) comparator_22 (
    .a(comtype), .b(3'b001), .gt(comparator_22_gt));  // open: eq, lt
  Comparator #(.width(3)) comparator_23 (.a(comtype), .b(3'b000), .eq(comparator_23_eq));  // open: gt, lt
  Comparator #(.width(3)) comparator_24 (.a(command[14:12]), .b(3'b000), .eq(comparator_24_eq));  // open: gt, lt
  Comparator #(.width(7)) comparator_25 (.a(command[31:25]), .b(7'b0100000), .eq(comparator_25_eq));  // open: gt, lt
  Comparator #(.width(3)) comparator_26 (.a(comtype), .b(3'b000), .eq(comparator_26_eq));  // open: gt, lt
  Comparator #(.width(3)) comparator_27 (.a(command[14:12]), .b(3'b000), .eq(comparator_27_eq));  // open: gt, lt
  Comparator #(.width(7)) comparator_28 (.a(command[31:25]), .b(7'b0000001), .eq(comparator_28_eq));  // open: gt, lt
  Comparator #(.width(3)) comparator_29 (.a(comtype), .b(3'b000), .eq(comparator_29_eq));  // open: gt, lt
  Comparator #(.width(3)) comparator_30 (.a(command[14:12]), .b(3'b011), .eq(comparator_30_eq));  // open: gt, lt
  Comparator #(.width(7)) comparator_31 (.a(command[31:25]), .b(7'b0000001), .eq(comparator_31_eq));  // open: gt, lt
  Comparator #(.width(3)) comparator_32 (.a(comtype), .b(3'b000), .eq(comparator_32_eq));  // open: gt, lt
  Comparator #(.width(3)) comparator_33 (.a(command[14:12]), .b(3'b001), .eq(comparator_33_eq));  // open: gt, lt
  Comparator #(.width(7)) comparator_34 (.a(command[31:25]), .b(7'b0000001), .eq(comparator_34_eq));  // open: gt, lt
  Comparator #(.width(3)) comparator_35 (.a(comtype), .b(3'b000), .eq(comparator_35_eq));  // open: gt, lt
  Comparator #(.width(3)) comparator_36 (.a(command[14:12]), .b(3'b101), .eq(comparator_36_eq));  // open: gt, lt
  Comparator #(.width(7)) comparator_37 (.a(command[31:25]), .b(7'b0000001), .eq(comparator_37_eq));  // open: gt, lt
  Comparator #(.width(3)) comparator_38 (.a(comtype), .b(3'b000), .eq(comparator_38_eq));  // open: gt, lt
  Comparator #(.width(3)) comparator_39 (.a(command[14:12]), .b(3'b100), .eq(comparator_39_eq));  // open: gt, lt
  Comparator #(.width(7)) comparator_40 (.a(command[31:25]), .b(7'b0000001), .eq(comparator_40_eq));  // open: gt, lt
  Comparator #(.width(3)) comparator_41 (.a(comtype), .b(3'b000), .eq(comparator_41_eq));  // open: gt, lt
  Comparator #(.width(3)) comparator_42 (.a(command[14:12]), .b(3'b111), .eq(comparator_42_eq));  // open: gt, lt
  Comparator #(.width(7)) comparator_43 (.a(command[31:25]), .b(7'b0000001), .eq(comparator_43_eq));  // open: gt, lt
  Comparator #(.width(3)) comparator_44 (.a(comtype), .b(3'b000), .eq(comparator_44_eq));  // open: gt, lt
  Comparator #(.width(3)) comparator_45 (.a(command[14:12]), .b(3'b101), .eq(comparator_45_eq));  // open: gt, lt
  Comparator #(.width(7)) comparator_46 (.a(command[31:25]), .b({7{1'b0}}), .eq(comparator_46_eq));  // open: gt, lt
  Comparator #(.width(7)) comparator_47 (.a(command[6:0]), .b(7'b0010011), .eq(comparator_47_eq));  // open: gt, lt
  Comparator #(.width(3)) comparator_48 (.a(command[14:12]), .b(3'b101), .eq(comparator_48_eq));  // open: gt, lt
  Comparator #(.width(7)) comparator_49 (.a(command[6:0]), .b(7'b0010011), .eq(comparator_49_eq));  // open: gt, lt
  Comparator #(.width(3)) comparator_50 (.a(command[14:12]), .b(3'b010), .eq(comparator_50_eq));  // open: gt, lt
  Comparator #(.width(3)) comparator_51 (.a(comtype), .b(3'b000), .eq(comparator_51_eq));  // open: gt, lt
  Comparator #(.width(3)) comparator_52 (.a(command[14:12]), .b(3'b001), .eq(comparator_52_eq));  // open: gt, lt
  Comparator #(.width(7)) comparator_53 (.a(command[31:25]), .b({7{1'b0}}), .eq(comparator_53_eq));  // open: gt, lt
  Comparator #(.width(7)) comparator_54 (.a(command[6:0]), .b(7'b0010011), .eq(comparator_54_eq));  // open: gt, lt
  Comparator #(.width(3)) comparator_55 (.a(command[14:12]), .b(3'b001), .eq(comparator_55_eq));  // open: gt, lt
  Comparator #(.width(7)) comparator_56 (.a(command[31:25]), .b({7{1'b0}}), .eq(comparator_56_eq));  // open: gt, lt
  and and_2 (and_2_out, comparator_54_eq, comparator_55_eq);
  typeDiver typediver_1 (.COMMAND(command), .opcodeType(comtype));
  and and_3 (and_3_out, comparator_1_eq, comparator_2_eq);
  and and_4 (and_4_out, comparator_4_eq, comparator_5_eq);
  and and_5 (and_5_out, comparator_6_eq, comparator_7_eq);
  and and_6 (and_6_out, comparator_9_eq, comparator_10_eq);
  and and_7 (and_7_out, comparator_11_eq, comparator_12_eq);
  and and_8 (and_8_out, comparator_14_eq, comparator_15_eq);
  and and_9 (and_9_out, comparator_16_eq, comparator_17_eq);
  and and_10 (and_10_out, comparator_19_eq, comparator_20_eq);
  and and_11 (and_11_out, comparator_23_eq, comparator_24_eq);
  and and_12 (and_12_out, comparator_26_eq, comparator_27_eq);
  and and_13 (and_13_out, comparator_29_eq, comparator_30_eq);
  and and_14 (and_14_out, comparator_32_eq, comparator_33_eq);
  and and_15 (and_15_out, comparator_35_eq, comparator_36_eq);
  and and_16 (and_16_out, comparator_38_eq, comparator_39_eq);
  and and_17 (and_17_out, comparator_41_eq, comparator_42_eq);
  and and_18 (and_18_out, comparator_44_eq, comparator_45_eq);
  and and_19 (and_19_out, comparator_51_eq, comparator_52_eq);
  and and_20 (and_20_out, and_3_out, comparator_3_eq);
  and and_21 (and_21_out, and_5_out, comparator_8_eq);
  and and_22 (and_22_out, and_7_out, comparator_13_eq);
  and and_23 (and_23_out, and_9_out, comparator_18_eq);
  and and_24 (subs, and_11_out, comparator_25_eq);
  and and_25 (mults, and_12_out, comparator_28_eq);
  and and_26 (mulhus, and_13_out, comparator_31_eq);
  and and_27 (mulhs, and_14_out, comparator_34_eq);
  and and_28 (divus, and_15_out, comparator_37_eq);
  and and_29 (divs, and_16_out, comparator_40_eq);
  and and_30 (remus, and_17_out, comparator_43_eq);
  and and_31 (and_31_out, and_18_out, comparator_46_eq);
  and and_32 (and_32_out, and_19_out, comparator_53_eq);
  and and_33 (and_33_out, and_2_out, comparator_56_eq);
  or or_1 (or_1_out, comparator_21_eq, comparator_22_gt);
  Comparator #(.width(7)) comparator_57 (.a(command[6:0]), .b(7'b0110111), .eq(comparator_57_eq));  // open: gt, lt
  and and_34 (and_34_out, comparator_47_eq, comparator_48_eq);
  and and_35 (slts, comparator_49_eq, comparator_50_eq);
  or or_2 (ands, and_20_out, and_4_out);
  or or_3 (ors, and_21_out, and_6_out);
  or or_4 (xors, and_22_out, and_8_out);
  or or_5 (or_5_out, and_23_out, and_10_out);
  or or_6 (slls, and_32_out, and_33_out);
  or or_7 (adds, or_5_out, or_8_out);
  or or_8 (or_8_out, or_1_out, comparator_57_eq);
  or or_9 (srls, and_31_out, and_34_out);
  Priority_Encoder #(.select(4)) priority_encoder_1 (
    .in0(ands), .in1(ors), .in2(xors), .in3(adds), .in4(subs), .in5(mults), .in6(mulhus), .in7(mulhs),
    .in8(divus), .in9(divs), .in10(remus), .in11(srls), .in13(slts), .in15(slls), .out(alusel));  // open: in12, in14, gs, en_out, en_in

  // Other names for the same wires on the sheet: com[31:0] = command; opcode[6:0] = command[6:0];
  //   fun3[2:0] = command[14:12]; fun7[6:0] = command[31:25]
endmodule

module fixlui (
  input  [31:0] command,
  output luio
);

  wire comparator_1_eq, comparator_1_gt, comparator_1_lt;

  Comparator #(.width(7)) comparator_1 (
    .a(command[6:0]), .b(7'b0110111), .gt(comparator_1_gt), .eq(comparator_1_eq), .lt(comparator_1_lt));
  Comparator #(.width(7)) comparator_2 (
    .a(command[6:0]), .b(7'b0110111), .gt(comparator_1_gt), .eq(comparator_1_eq), .lt(comparator_1_lt));
  not not_1 (luio, comparator_1_eq);
  not not_2 (luio, comparator_1_eq);

  // Other names for the same wires on the sheet: com[31:0] = command; opcode[6:0] = command[6:0];
  //   fun3[2:0] = command[14:12]; fun7[6:0] = command[31:25]
endmodule

module wbsel (
  input  [31:0] command,
  input  clock,
  input  ifbtrue,
  output [1:0] wbsel
);

  wire and_1_out, and_2_out, comparator_1_eq, comparator_2_eq, comparator_3_eq, comparator_4_eq,
       comparator_5_eq, nor_1_out, not_1_out, or_1_out, or_2_out;

  Comparator #(.width(7)) comparator_1 (.a(command[6:0]), .b(7'b0000011), .eq(comparator_1_eq));  // open: gt, lt
  Comparator #(.width(7)) comparator_2 (.a(command[6:0]), .b(7'b1100011), .eq(comparator_2_eq));  // open: gt, lt
  not not_1 (not_1_out, ifbtrue);
  Comparator #(.width(7)) comparator_3 (.a(command[6:0]), .b(7'b1101111), .eq(comparator_3_eq));  // open: gt, lt
  Comparator #(.width(7)) comparator_4 (.a(command[6:0]), .b(7'b1100111), .eq(comparator_4_eq));  // open: gt, lt
  Comparator #(.width(3)) comparator_5 (.a(command[14:12]), .b(3'b000), .eq(comparator_5_eq));  // open: gt, lt
  and and_1 (and_1_out, comparator_2_eq, not_1_out);
  or or_1 (or_1_out, and_1_out, comparator_3_eq);
  and and_2 (and_2_out, comparator_4_eq, comparator_5_eq);
  or or_2 (or_2_out, or_1_out, and_2_out);
  nor nor_1 (nor_1_out, comparator_1_eq, or_2_out);
  Priority_Encoder #(.select(2)) priority_encoder_1 (
    .in0(comparator_1_eq), .in1(nor_1_out), .in2(or_2_out), .out(wbsel));  // open: in3, gs, en_out, en_in

  // Other names for the same wires on the sheet: com[31:0] = command; opcode[6:0] = command[6:0];
  //   fun3[2:0] = command[14:12]; fun7[6:0] = command[31:25]
endmodule

module regwen (
  input  [31:0] in_1,
  output regwen
);

  wire comparator_1_eq, comparator_2_eq, or_1_out;

  Comparator #(.width(7)) comparator_1 (.a(in_1[6:0]), .b(7'b0100011), .eq(comparator_1_eq));  // open: gt, lt
  Comparator #(.width(7)) comparator_2 (.a(in_1[6:0]), .b(7'b1100011), .eq(comparator_2_eq));  // open: gt, lt
  or or_1 (or_1_out, comparator_1_eq, comparator_2_eq);
  not not_1 (regwen, or_1_out);

  // Other names for the same wires on the sheet: com[31:0] = in_1; opcode[6:0] = in_1[6:0]; fun3[2:0] = in_1[14:12];
  //   fun7[6:0] = in_1[31:25]
endmodule

module nextAddress (
  input  [31:0] command,
  input  isBtrue,
  output isAlu2PC
);

  wire and_1_out, comparator_1_eq, comparator_2_eq, comparator_3_eq, or_1_out;

  Comparator #(.width(7)) comparator_1 (.a(command[6:0]), .b(7'b1100111), .eq(comparator_1_eq));  // open: gt, lt
  Comparator #(.width(7)) comparator_2 (.a(command[6:0]), .b(7'b1101111), .eq(comparator_2_eq));  // open: gt, lt
  Comparator #(.width(7)) comparator_3 (.a(command[6:0]), .b(7'b1100011), .eq(comparator_3_eq));  // open: gt, lt
  or or_1 (or_1_out, comparator_2_eq, comparator_1_eq);
  and and_1 (and_1_out, comparator_3_eq, isBtrue);
  or or_2 (isAlu2PC, or_1_out, and_1_out);

  // Other names for the same wires on the sheet: com[31:0] = command; opcode[6:0] = command[6:0];
  //   fun3[2:0] = command[14:12]; fun7[6:0] = command[31:25]

  // Notes on the sheet:
  //   jal
  //   jalr
  //   jal
endmodule

module isWriteRAMEn (
  input  [31:0] command,
  output isWriteRAMEN
);

  Comparator #(.width(7)) comparator_1 (.a(command[6:0]), .b(7'b0100011), .eq(isWriteRAMEN));  // open: gt, lt

  // Other names for the same wires on the sheet: com[31:0] = command; opcode[6:0] = command[6:0];
  //   fun3[2:0] = command[14:12]; fun7[6:0] = command[31:25]

  // Notes on the sheet:
  //   sw
endmodule

module fixJumpAdd (
  input  [31:0] command,
  input  isPCtaken,
  output isFixAdd
);

  wire comparator_1_eq, not_1_out;
  wire [2:0] comtype;

  Comparator #(.width(3)) comparator_1 (.a(comtype), .b(3'b100), .eq(comparator_1_eq));  // open: gt, lt
  not not_1 (not_1_out, comparator_1_eq);
  typeDiver typediver_1 (.COMMAND(command), .opcodeType(comtype));
  and and_1 (isFixAdd, not_1_out, isPCtaken);

  // Other names for the same wires on the sheet: com[31:0] = command; opcode[6:0] = command[6:0];
  //   fun3[2:0] = command[14:12]; fun7[6:0] = command[31:25]
endmodule

module dropInvaildCommand (
  input  [31:0] command,
  input  isJump,
  output [31:0] VaildCommand
);

  Multiplexer #(.width(32), .enable("false")) multiplexer_1 (
    .in0(command), .in1(32'h33), .out(VaildCommand), .sel(isJump));
endmodule

module fixRa (
  input  [31:0] rs1data,
  input  [31:0] Command,
  output [31:0] rs1fixRa
);

  wire comparator_1_eq;
  wire [2:0] comtype;
  wire [31:0] shifter_1_out;

  Comparator #(.width(7)) comparator_1 (.a(Command[6:0]), .b(7'b1100111), .eq(comparator_1_eq));  // open: gt, lt
  Shifter #(.width(32), .shift("ar")) shifter_1 (.in(rs1data), .\dist (5'b00010), .out(shifter_1_out));
  typeDiver typediver_1 (.COMMAND(Command), .opcodeType(comtype));
  Multiplexer #(.width(32), .enable("false")) multiplexer_1 (
    .in0(rs1data), .in1(shifter_1_out), .out(rs1fixRa), .sel(comparator_1_eq));

  // Other names for the same wires on the sheet: com[31:0] = Command; opcode[6:0] = Command[6:0];
  //   fun3[2:0] = Command[14:12]; fun7[6:0] = Command[31:25]
endmodule

module loadRAMnotWordFix (
  input  [31:0] command,
  input  [31:0] RAMData,
  output [31:0] loadData
);

  wire [31:0] byteSign, byteUnsign, halfSign, halfUnsign;

  assign halfUnsign = {{16{1'b0}}, RAMData[15:0]};  // Bit_Extender bit_extender_1
  assign halfSign = {{16{RAMData[15]}}, RAMData[15:0]};  // Bit_Extender bit_extender_2
  assign byteUnsign = {{24{1'b0}}, RAMData[7:0]};  // Bit_Extender bit_extender_3
  assign byteSign = {{24{RAMData[7]}}, RAMData[7:0]};  // Bit_Extender bit_extender_4
  Multiplexer #(.select(3), .width(32), .enable("false")) multiplexer_1 (
    .in0(byteSign), .in1(halfSign), .in2(RAMData), .in4(byteUnsign), .in5(halfUnsign), .out(loadData),
    .sel(command[14:12]));  // open: in3, in6, in7

  // Other names for the same wires on the sheet: com[31:0] = command; opcode[6:0] = command[6:0];
  //   fun3[2:0] = command[14:12]; fun7[6:0] = command[31:25]; word[31:0] = RAMData
endmodule

module isauipc (
  input  [31:0] command,
  output isauipc
);

  Comparator #(.width(7)) comparator_1 (.a(7'b0010111), .b(command[6:0]), .eq(isauipc));  // open: gt, lt

  // Other names for the same wires on the sheet: com[31:0] = command; opcode[6:0] = command[6:0];
  //   fun3[2:0] = command[14:12]; fun7[6:0] = command[31:25]
endmodule
